# Fritzing sketch Receiver (saved by Fritzing 0.9.2b)
breadboards: 1

parts:
  Part1 = Arduino Nano (Rev3.0) (ICSP)
  Grove1 = Grove OLED 128x96
  U1 = RF-LINK_TX [package=rf-link_tx]

nets:
  GND: Part1.GND, Grove1.GND, U1.GND
  5V: Part1.5V, Grove1.VCC, U1.+5V
  N1: Part1.A5, Grove1.SCL
  N2: Part1.A4, Grove1.SDA
  N3: Part1.D11/MOSI, U1.DATA

notes:
  Use the RF receiver here
