# Fritzing sketch Transmitter (saved by Fritzing 0.9.2b)
circuit board: 8.46667cm x 5.64444cm
breadboards: 1

parts:
  U1 = RF-LINK_TX [package=rf-link_tx]
  Part1 = Arduino Nano (Rev3.0) (ICSP)
  RHT1 = Humidity and Temperature Sensor RHT03

nets:
  N1: U1.DATA, Part1.D11/MOSI
  GND: U1.GND, Part1.GND, RHT1.GND_2
  +5V: U1.+5V, Part1.5V, RHT1.Vcc
  N2: Part1.D9, RHT1.Data-signal
